// Logisim project lab2.circ as structural Verilog: 6 circuits, main circuit Circuit_1_com
module Circuit_1_com (
  input  [1:0] A,
  input  [1:0] B,
  output result
);

  wire and_1_out, and_2_out, and_3_out, and_4_out, and_5_out, not_1_out, not_2_out, not_3_out, not_4_out,
       not_5_out;

  not not_1 (not_1_out, A[0]);
  and and_1 (and_1_out, not_1_out, not_2_out);
  not not_2 (not_2_out, A[1]);
  not not_3 (not_3_out, A[0]);
  and and_2 (and_2_out, not_3_out, B[1]);
  not not_4 (not_4_out, A[0]);
  and and_3 (and_3_out, not_4_out, B[0]);
  not not_5 (not_5_out, A[1]);
  and and_4 (and_4_out, not_5_out, B[0]);
  and and_5 (and_5_out, B[0], B[1]);
  or or_1 (result, and_1_out, and_2_out, and_3_out, and_4_out, and_5_out);
endmodule

module Circuit_1_Multiplexer (
  input  [1:0] A,
  input  [1:0] B,
  output result_2
);

  Multiplexer #(.select(4), .enable("false")) multiplexer_1 (
    .in0(1'b1), .in1(1'b1), .in2(1'b1), .in3(1'b1), .in4(1'b0), .in5(1'b1), .in6(1'b1), .in7(1'b1),
    .in8(1'b0), .in9(1'b0), .in10(1'b1), .in11(1'b1), .in12(1'b0), .in13(1'b0), .in14(1'b0), .in15(1'b1),
    .out(result_2), .sel({A, B}));
endmodule

module Circuit_1_Rom (
  input  [1:0] a,
  input  [1:0] b,
  input  in_3,
  output Result
);

  ROM #(.addrWidth(4), .dataWidth(1)) rom_1 (.addr({a, b}), .data(Result), .sel(in_3));

  // Notes on the sheet:
  //   contents of rom_1 (hex, n*v repeats v):
  //   4*1 0 1 1 1 0 0 1 1 0 0 0 1
endmodule

module Circuit_2_com (
  input  X,
  input  Y,
  input  Z,
  output result
);

  wire and_1_out, and_2_out, and_3_out, not_1_out, not_2_out, not_3_out, not_4_out, not_5_out, not_6_out;

  not not_1 (not_1_out, X);
  not not_2 (not_2_out, Y);
  not not_3 (not_3_out, X);
  not not_4 (not_4_out, Z);
  not not_5 (not_5_out, Y);
  not not_6 (not_6_out, Z);
  and and_1 (and_1_out, not_1_out, not_2_out);
  and and_2 (and_2_out, not_3_out, not_4_out);
  and and_3 (and_3_out, not_5_out, not_6_out);
  or or_1 (result, and_1_out, and_2_out, and_3_out);
endmodule

module Circuit_2_Multiplexer (
  input  Z,
  input  Y,
  input  X,
  output Output
);

  Multiplexer #(.select(3), .enable("false")) multiplexer_1 (
    .in0(1'b1), .in1(1'b1), .in2(1'b1), .in3(1'b0), .in4(1'b1), .in5(1'b0), .in6(1'b0), .in7(1'b0),
    .out(Output), .sel({X, Y, Z}));

  // Notes on the sheet:
  //   Constants
  //   Values
endmodule

module Circuit_2_Rom (
  input  Z,
  input  Y,
  input  X,
  input  Selector,
  output out_5
);

  ROM #(.addrWidth(3), .dataWidth(1)) rom_1 (.addr({X, Y, Z}), .data(out_5), .sel(Selector));

  // Notes on the sheet:
  //   contents of rom_1 (hex, n*v repeats v):
  //   1 1 1 0 1
endmodule
